// Logisim project 8bit_cpu2.circ as structural Verilog: 2 circuits, main circuit main
module main (
  input  in_1
);

  wire A_TO_BUS, A_WRITE, ADD_C, adder_1_cout, ALU_TO_A, BUS_TO_A, BUS_TO_COUNTER, CARRY, comparator_1_eq,
       controlled_buffer_1_out, controlled_buffer_12_out, COUNTER_ENABLE, COUNTER_LOAD, COUNTER_MAIN, D4_LOD,
       D8_LOD, demultiplexer_1_out0, demultiplexer_1_out1, demultiplexer_1_out2, demultiplexer_1_out3,
       demultiplexer_1_out4, demultiplexer_1_out5, demultiplexer_1_out6, demultiplexer_1_out7,
       demultiplexer_1_out8, demultiplexer_1_out12, demultiplexer_1_out13, digital_oscilloscope_1_p1,
       or_1_out, OUT_3_WRITE, REG_IN, REG_OUT, REG_WRITE, SUB_C, subtractor_1_bout, undriven, undriven_2,
       undriven_3, ZERO;
  wire [0:0] PROGRAM_DECODER_out;
  wire [1:0] ALU_CH;
  wire [7:0] A_DATA, adder_1_out, and_1_out, B_DATA, controlled_buffer_7_out, controlled_buffer_8_out, IN1_q,
       IN2_q, INPUT_1, INPUT_2, multiplexer_1_out, multiplexer_2_out, OUTPUT_1, OUTPUT_2, R0_q, R1_q, R2_q,
       R3_q, R4_q, R5_q, R6_q, R7_q, subtractor_1_out, T_H_q, T_M_q, T_S_q, xor_1_out;
  wire [9:0] counter_1_q;
  wire [11:0] controlled_buffer_2_out, controlled_buffer_3_out, OUTPUT_3, rom_1_data, TIME_1_q;

  // Digital_Oscilloscope digital_oscilloscope_1: pin names not known; wires that end beside it: digital_oscilloscope_1_p1
  Comparator #(.width(2)) comparator_1 (.a(counter_1_q[5:4]), .b(2'b10), .eq(comparator_1_eq));  // open: gt, lt
  _7_Segment_Display u_7_segment_display_1 ();  // open: g, f, a, b, e, d, c, dp
  // BCD_to_7_Segment_decoder bcd_to_7_segment_decoder_1: pin names not known
  // Binary_to_BCD_converter #(.binvalue(8)) binary_to_bcd_converter_1: pin names not known; wires that end beside it: A_DATA
  _7_Segment_Display u_7_segment_display_2 ();  // open: g, f, a, b, e, d, c, dp
  // BCD_to_7_Segment_decoder bcd_to_7_segment_decoder_2: pin names not known
  _7_Segment_Display u_7_segment_display_3 ();  // open: g, f, a, b, e, d, c, dp
  // BCD_to_7_Segment_decoder bcd_to_7_segment_decoder_3: pin names not known
  TTY tty_1 (.data(OUTPUT_1[7:1]), .clk(comparator_1_eq), .we(OUTPUT_1[0]), .clr(or_1_out));
  or or_1 (or_1_out, OUTPUT_2[0], in_1);
  // LedBar #(.inputtype("row"), .matrixcols(7)) ledbar_1: pin names not known; wires that end beside it: OUTPUT_3, OUTPUT_1[7:1], INPUT_2
  Counter #(.max('h2), .width(2)) counter_1 (
    .Q(counter_1_q[5:4]), .clk(COUNTER_MAIN), .clr(digital_oscilloscope_1_p1));  // open: load, D, count, carry, up
  Keyboard keyboard_1 (.clk(comparator_1_eq), .avail(INPUT_1[0]), .data(INPUT_1[7:1]));  // open: re, clr
  // LedBar #(.inputtype("row"), .matrixcols(2)) ledbar_2: pin names not known; wires that end beside it: counter_1_q[5:4]
  Comparator comparator_2 (.a(A_DATA), .b(B_DATA), .gt(counter_1_q[2]), .eq(counter_1_q[1]), .lt(counter_1_q[0]));
  Clock clock_1 (.out(COUNTER_MAIN));
  or or_2 (digital_oscilloscope_1_p1, PROGRAM_DECODER_out[0], in_1);
  PLA #(.in_width(10), .out_width(16), .\table ("0000xxxxxx 1000000000000001 # none\n0000xxxxxx 1000000000000001 # none\n0000xxxxxx 1000000000000001 # none\n000100xxxx 0001100000000000 # jump\n000101xxxx 1111100000000000 # jump\n000110xxxx 1000000000000001 # jump\n001000x1xx 0001100000000000 # jump>\n001001x1xx 1111100000000000 # jump>\n001010x1xx 1000000000000001 # jump>\n001000x0xx 1000000000000000 # jump>\n001001x0xx 1000000000000000 # jump>\n001010x0xx 1000000000000001 # jump>\n001100xx1x 0001100000000000 # jump=\n001101xx1x 1111100000000000 # jump=\n001110xx1x 1000000000000001 # jump=\n001100xx0x 1000000000000000 # jump=\n001101xx0x 1000000000000000 # jump=\n001110xx0x 1000000000000001 # jump=\n010000xxx1 0001100000000000 # jump<\n010001xxx1 1111100000000000 # jump<\n010010xxx1 1000000000000001 # jump<\n010000xxx0 1000000000000000 # jump<\n010001xxx0 1000000000000000 # jump<\n010010xxx0 1000000000000001 # jump<\n010100xxxx 0001100000000000 # DATA TO A\n010101xxxx 0001100000011000 # DATA TO A\n010110xxxx 1000000000000000 # DATA TO A\n011000xxxx 0001100000000000 # DATA TO RAM\n011001xxxx 0001110100000000 # DATA TO RAM\n011010xxxx 1000000000000000 # DATA TO RAM\n011100xxxx 0001000000000000 # A TO RAM\n011101xxxx 0001010100000010 # A TO RAM\n011110xxxx 1000000000000000 # A TO RAM\n100000xxxx 0000000000010100 # ADD\n100001xxxx 0000000000010100 # ADD\n100010xxxx 1000000000000000 # ADD\n100100xxxx 0000000001000000 # MINUS\n100101xxxx 0000000001010100 # MINUS\n100110xxxx 1000000000000000 # MINUS\n101000xxxx 0000000010000000 # AND\n101001xxxx 0000000010010100 # AND\n101010xxxx 1000000000000000 # AND\n101100xxxx 0000000011000000 # XOR\n101101xxxx 0000000011010100 # XOR\n101110xxxx 1000000000000000 # XOR\n110000xxxx 0001001000000000 # RAM TO A\n110010xxxx 0001001000011000 # RAM TO A\n110001xxxx 1000000000000000 # RAM TO A\n1101001xxx 0001100000000000 # JUMP IF ZERO\n1101011xxx 1111100000000000 # JUMP IF ZERO\n1101101xxx 1000000000000001 # JUMP IF ZERO\n1101000xxx 1000000000000000 # JUMP IF  ZERO\n1101010xxx 1000000000000000 # JUMP IF  ZERO\n1101100xxx 1000000000000001 # JUMP IF  ZERO\n1110000xxx 0001100000000000 # JUMP IF NO ZERO\n1110010xxx 1111100000000000 # JUMP IF NO ZERO\n1110100xxx 1000000000000001 # JUMP IF NO ZERO\n1110001xxx 1000000000000000 # JUMP IF  NO ZERO\n1110011xxx 1000000000000000 # JUMP IF  NO ZERO\n1110101xxx 1000000000000001 # JUMP IF  NO ZERO\n111000xxxx 0001100000000000 # LOAD DATA to OUT\n111101xxxx 0001100000100000 # LOAD DATA to OUT\n111110xxxx 1000000000000000 # LOAD DATA to OUT")) PROGRAM_DECODER (
    .in({counter_1_q[9:4], ZERO, counter_1_q[2:0]}),
    .out({COUNTER_ENABLE, COUNTER_LOAD, BUS_TO_COUNTER, D4_LOD, D8_LOD, REG_IN, REG_OUT, REG_WRITE, ALU_CH[0], ALU_CH[1], OUT_3_WRITE, A_WRITE, BUS_TO_A, ALU_TO_A, A_TO_BUS, PROGRAM_DECODER_out[0]}));
  Counter #(.max('hfff), .width(12)) TIME_1 (
    .clr(in_1), .load(COUNTER_LOAD), .clk(controlled_buffer_1_out), .D(controlled_buffer_2_out), .Q(TIME_1_q));  // open: up, count, carry
  assign controlled_buffer_1_out = COUNTER_ENABLE ? COUNTER_MAIN : 1'bz;  // Controlled_Buffer controlled_buffer_1
  ROM #(.addrWidth(12), .dataWidth(16)) rom_1 (.addr(TIME_1_q), .data({counter_1_q[9:6], rom_1_data}));
  assign controlled_buffer_2_out = BUS_TO_COUNTER ? controlled_buffer_3_out : 12'bz;  // Controlled_Buffer controlled_buffer_2
  assign controlled_buffer_3_out[11:8] = D4_LOD ? rom_1_data[11:8] : 4'bz;  // Controlled_Buffer controlled_buffer_3
  // LedBar #(.inputtype("row"), .matrixcols(4)) ledbar_3: pin names not known; wires that end beside it: counter_1_q[9:6]
  assign controlled_buffer_3_out[7:0] = D8_LOD ? rom_1_data[7:0] : 8'bz;  // Controlled_Buffer controlled_buffer_4
  // LedBar #(.inputtype("row"), .matrixcols(4)) ledbar_4: pin names not known; wires that end beside it: controlled_buffer_3_out[11:8]
  assign controlled_buffer_3_out[7:0] = REG_OUT ? multiplexer_1_out : 8'bz;  // Controlled_Buffer controlled_buffer_5
  // LedBar #(.inputtype("row")) ledbar_5: pin names not known; wires that end beside it: controlled_buffer_3_out[7:0]
  assign controlled_buffer_3_out[7:0] = A_TO_BUS ? A_DATA : 8'bz;  // Controlled_Buffer controlled_buffer_6
  assign controlled_buffer_7_out = REG_IN ? controlled_buffer_3_out[7:0] : 8'bz;  // Controlled_Buffer controlled_buffer_7
  assign controlled_buffer_8_out = BUS_TO_A ? controlled_buffer_3_out[7:0] : 8'bz;  // Controlled_Buffer controlled_buffer_8
  Register #(.width(12)) register_1 (
    .D({controlled_buffer_3_out[7:0], controlled_buffer_3_out[11:8]}), .en(OUT_3_WRITE), .clk(COUNTER_MAIN),
    .Q(OUTPUT_3), .clr(in_1));
  assign controlled_buffer_8_out = ALU_TO_A ? multiplexer_2_out : 8'bz;  // Controlled_Buffer controlled_buffer_9
  Register A (.D(controlled_buffer_8_out), .en(A_WRITE), .clk(COUNTER_MAIN), .Q(A_DATA), .clr(in_1));
  Multiplexer #(.select(4), .width(8)) multiplexer_1 (
    .in0(B_DATA), .in1(R0_q), .in2(R1_q), .in3(R2_q), .in4(R3_q), .in5(R4_q), .in6(R5_q), .in7(R6_q),
    .in8(R7_q), .in9(T_H_q), .in10(T_M_q), .in11(T_S_q), .in12(OUTPUT_1), .in13(OUTPUT_2), .in14(IN1_q),
    .in15(IN2_q), .out(multiplexer_1_out), .sel(controlled_buffer_3_out[11:8]));
  Demultiplexer #(.select(4)) demultiplexer_1 (
    .out0(demultiplexer_1_out0), .out1(demultiplexer_1_out1), .out2(demultiplexer_1_out2),
    .out3(demultiplexer_1_out3), .out4(demultiplexer_1_out4), .out5(demultiplexer_1_out5),
    .out6(demultiplexer_1_out6), .out7(demultiplexer_1_out7), .out8(demultiplexer_1_out8),
    .out12(demultiplexer_1_out12), .out13(demultiplexer_1_out13), .in(REG_WRITE),
    .sel(controlled_buffer_3_out[11:8]));  // open: out9, out10, out11, out14, out15
  Register B (
    .D(controlled_buffer_7_out), .en(demultiplexer_1_out0), .clk(controlled_buffer_12_out), .Q(B_DATA),
    .clr(in_1));
  Adder adder_1 (.a(A_DATA), .b(B_DATA), .out(adder_1_out), .cout(adder_1_cout));  // open: cin
  Subtractor subtractor_1 (.a(A_DATA), .b(B_DATA), .out(subtractor_1_out), .bout(subtractor_1_bout));  // open: bin
  assign and_1_out = A_DATA & B_DATA;  // AND_Gate and_1, 8 bits wide
  assign xor_1_out = A_DATA ^ B_DATA;  // XOR_Gate xor_1, 8 bits wide
  Register R0 (
    .D(controlled_buffer_7_out), .en(demultiplexer_1_out1), .clk(controlled_buffer_12_out), .Q(R0_q),
    .clr(in_1));
  Register R1 (
    .D(controlled_buffer_7_out), .en(demultiplexer_1_out2), .clk(controlled_buffer_12_out), .Q(R1_q),
    .clr(in_1));
  Multiplexer #(.select(2), .width(8)) multiplexer_2 (
    .in0(adder_1_out), .in1(subtractor_1_out), .in2(and_1_out), .in3(xor_1_out), .out(multiplexer_2_out),
    .sel(ALU_CH));
  assign CARRY = ADD_C ? subtractor_1_bout : 1'bz;  // Controlled_Buffer controlled_buffer_10
  Register R2 (
    .D(controlled_buffer_7_out), .en(demultiplexer_1_out3), .clk(controlled_buffer_12_out), .Q(R2_q),
    .clr(in_1));
  Comparator comparator_3 (.a(A_DATA), .b({8{1'b0}}), .eq(ZERO));  // open: gt, lt
  assign CARRY = SUB_C ? adder_1_cout : 1'bz;  // Controlled_Buffer controlled_buffer_11
  Register R3 (
    .D(controlled_buffer_7_out), .en(demultiplexer_1_out4), .clk(controlled_buffer_12_out), .Q(R3_q),
    .clr(in_1));
  Register R4 (
    .D(controlled_buffer_7_out), .en(demultiplexer_1_out5), .clk(controlled_buffer_12_out), .Q(R4_q),
    .clr(in_1));
  Register R5 (
    .D(controlled_buffer_7_out), .en(demultiplexer_1_out6), .clk(controlled_buffer_12_out), .Q(R5_q),
    .clr(in_1));
  Register R6 (
    .D(controlled_buffer_7_out), .en(demultiplexer_1_out7), .clk(controlled_buffer_12_out), .Q(R6_q),
    .clr(in_1));
  Register R7 (
    .D(controlled_buffer_7_out), .en(demultiplexer_1_out8), .clk(controlled_buffer_12_out), .Q(R7_q),
    .clr(in_1));
  Register T_H (.D(controlled_buffer_7_out), .en(undriven), .clk(controlled_buffer_12_out), .Q(T_H_q), .clr(in_1));
  Register T_M (.D(controlled_buffer_7_out), .en(undriven_2), .clk(controlled_buffer_12_out), .Q(T_M_q), .clr(in_1));
  Register T_S (.D(controlled_buffer_7_out), .en(undriven_3), .clk(controlled_buffer_12_out), .Q(T_S_q), .clr(in_1));
  Register OUT1 (
    .D(controlled_buffer_7_out), .en(demultiplexer_1_out12), .clk(controlled_buffer_12_out), .Q(OUTPUT_1),
    .clr(in_1));
  Register OUT2 (
    .D(controlled_buffer_7_out), .en(demultiplexer_1_out13), .clk(controlled_buffer_12_out), .Q(OUTPUT_2),
    .clr(in_1));
  Register IN1 (.D(INPUT_1), .en(controlled_buffer_12_out), .clk(controlled_buffer_12_out), .Q(IN1_q), .clr(in_1));
  Register IN2 (.D(INPUT_2), .en(controlled_buffer_12_out), .clk(controlled_buffer_12_out), .Q(IN2_q), .clr(in_1));
  assign controlled_buffer_12_out = REG_WRITE ? COUNTER_MAIN : 1'bz;  // Controlled_Buffer controlled_buffer_12

  // Other names for the same wires on the sheet: RESET = in_1

  // Notes on the sheet:
  //   contents of rom_1 (hex, n*v repeats v):
  //   0 5011 6001 b000 7c00 5000 d034 9*0 1000 35*0 d010 e038 0 0 1aaa
endmodule

module regr (
  input  [7:0] data_in,
  input  counter,
  input  reset,
  input  write,
  input  [3:0] address,
  output [7:0] data_out
);

  wire demultiplexer_1_out0, demultiplexer_1_out1, demultiplexer_1_out2, demultiplexer_1_out3,
       demultiplexer_1_out4, demultiplexer_1_out5, demultiplexer_1_out6, demultiplexer_1_out7,
       demultiplexer_1_out8, demultiplexer_1_out9, demultiplexer_1_out10, demultiplexer_1_out11,
       demultiplexer_1_out12, demultiplexer_1_out13, demultiplexer_1_out14, demultiplexer_1_out15;
  wire [7:0] register_1_q, register_2_q, register_3_q, register_4_q, register_5_q, register_6_q,
       register_7_q, register_8_q, register_9_q, register_10_q, register_11_q, register_12_q, register_13_q,
       register_14_q, register_15_q, register_16_q;

  Multiplexer #(.select(4), .width(8)) multiplexer_1 (
    .in0(register_1_q), .in1(register_2_q), .in2(register_3_q), .in3(register_4_q), .in4(register_5_q),
    .in5(register_6_q), .in6(register_7_q), .in7(register_8_q), .in8(register_9_q), .in9(register_10_q),
    .in10(register_11_q), .in11(register_12_q), .in12(register_13_q), .in13(register_14_q),
    .in14(register_15_q), .in15(register_16_q), .out(data_out), .sel(address));
  Demultiplexer #(.select(4)) demultiplexer_1 (
    .out0(demultiplexer_1_out0), .out1(demultiplexer_1_out1), .out2(demultiplexer_1_out2),
    .out3(demultiplexer_1_out3), .out4(demultiplexer_1_out4), .out5(demultiplexer_1_out5),
    .out6(demultiplexer_1_out6), .out7(demultiplexer_1_out7), .out8(demultiplexer_1_out8),
    .out9(demultiplexer_1_out9), .out10(demultiplexer_1_out10), .out11(demultiplexer_1_out11),
    .out12(demultiplexer_1_out12), .out13(demultiplexer_1_out13), .out14(demultiplexer_1_out14),
    .out15(demultiplexer_1_out15), .in(write), .sel(address));
  Register register_1 (.D(data_in), .en(demultiplexer_1_out0), .clk(counter), .Q(register_1_q), .clr(reset));
  Register register_2 (.D(data_in), .en(demultiplexer_1_out1), .clk(counter), .Q(register_2_q), .clr(reset));
  Register register_3 (.D(data_in), .en(demultiplexer_1_out2), .clk(counter), .Q(register_3_q), .clr(reset));
  Register register_4 (.D(data_in), .en(demultiplexer_1_out3), .clk(counter), .Q(register_4_q), .clr(reset));
  Register register_5 (.D(data_in), .en(demultiplexer_1_out4), .clk(counter), .Q(register_5_q), .clr(reset));
  Register register_6 (.D(data_in), .en(demultiplexer_1_out5), .clk(counter), .Q(register_6_q), .clr(reset));
  Register register_7 (.D(data_in), .en(demultiplexer_1_out6), .clk(counter), .Q(register_7_q), .clr(reset));
  Register register_8 (.D(data_in), .en(demultiplexer_1_out7), .clk(counter), .Q(register_8_q), .clr(reset));
  Register register_9 (.D(data_in), .en(demultiplexer_1_out8), .clk(counter), .Q(register_9_q), .clr(reset));
  Register register_10 (.D(data_in), .en(demultiplexer_1_out9), .clk(counter), .Q(register_10_q), .clr(reset));
  Register register_11 (.D(data_in), .en(demultiplexer_1_out10), .clk(counter), .Q(register_11_q), .clr(reset));
  Register register_12 (.D(data_in), .en(demultiplexer_1_out11), .clk(counter), .Q(register_12_q), .clr(reset));
  Register register_13 (.D(data_in), .en(demultiplexer_1_out12), .clk(counter), .Q(register_13_q), .clr(reset));
  Register register_14 (.D(data_in), .en(demultiplexer_1_out13), .clk(counter), .Q(register_14_q), .clr(reset));
  Register register_15 (.D(data_in), .en(demultiplexer_1_out14), .clk(counter), .Q(register_15_q), .clr(reset));
  Register register_16 (.D(data_in), .en(demultiplexer_1_out15), .clk(counter), .Q(register_16_q), .clr(reset));
endmodule
